# Fritzing sketch stewart-schematic (saved by Fritzing 1.0.4)
breadboards: 1

parts:
  J1 = 2.1mm Barrel Jack with Terminal Block
  PWM1 = PCA9685 16x12-bit PWM Breakout
  BAT2 = Battery Holders [package=lipo-1100mAh]
  J2 = Basic Servo
  J3 = Basic Servo
  J4 = Basic Servo
  J5 = Basic Servo
  J6 = Basic Servo
  J7 = Basic Servo
  A1 = Teensy 4.0

nets:
  VCC: J1.POS, PWM1.no_name_yet#100, PWM1.no_name_yet#101, PWM1.no_name_yet#102, PWM1.no_name_yet#103, PWM1.no_name_yet#104, PWM1.no_name_yet#105, PWM1.no_name_yet#506, PWM1.no_name_yet#706, BAT2.+, J3.vcc, J5.vcc, A1.pin33
  GND: J1.NEG, PWM1.no_name_yet#501, PWM1.no_name_yet#701, PWM1.no_name_yet#1000, PWM1.no_name_yet#1001, PWM1.no_name_yet#1002, PWM1.no_name_yet#1003, PWM1.no_name_yet#1004, PWM1.no_name_yet#1005, BAT2.-, J3.gnd, J5.gnd, A1.pin_1, A1.pin_32
  N1: PWM1.no_name_yet#0, J2.pulse
  N2: PWM1.no_name_yet#1, J3.pulse
  N3: PWM1.no_name_yet#2, J5.pulse
  N4: PWM1.no_name_yet#3, J6.pulse
  N5: PWM1.no_name_yet#4, J7.pulse
  N6: PWM1.no_name_yet#5, J4.pulse
  N7: PWM1.no_name_yet#503, A1.pin_26
  N8: PWM1.no_name_yet#504, A1.pin_25

custom parts:
  Teensy 4.0: The Teensy is a complete USB-based microcontoller development system, in a very small footprint, capable of implementing many types of projects. All programming is done via the USB port. No special programmer is needed, only a standard micro-USB cable and a PC or Macintosh with a USB port. (Oct 2023 added the VBUS pad at user request.)
